# Fritzing sketch ATMega328Programmer (saved by Fritzing 0.9.3b)
circuit board: 5.6471cm x 5.40592cm
breadboards: 1

parts:
  XTAL1 = Crystal [frequency="16 Mhz" package=THT]
  C1 = Ceramic Capacitor [capacitance=22pF package="100 mil [THT, multilayer]"]
  C2 = Ceramic Capacitor [capacitance=22pF package="100 mil [THT, multilayer]"]
  Arduino_Nano = Arduino Nano (Rev3.0)
  C3 = Electrolytic Capacitor [capacitance=10µF package="100 mil [THT, electrolytic]"]
  ZIF28 = atmega328 [package=dip]
  J3 = female pin header, 2 pins [form="♀ (female)"]
  J4 = female pin header, 2 pins [form="♀ (female)"]
  J5 = female pin header, 2 pins [form="♀ (female)"]
  J6 = female pin header, 2 pins [form="♀ (female)"]
  J2 = female pin header, 6 pins [form="♀ (female)"]
  J1 = female pin header, 4 pins [form="♀ (female)"]
  J7 = female pin header, 3 pins [form="♀ (female)"]

nets:
  N1: XTAL1.pin_0, C1.0, ZIF28.XLAT1
  N2: XTAL1.pin_1, C2.1, ZIF28.XLAT2
  N3: C1.1, C2.0, Arduino_Nano.GND, C3.-, ZIF28.GND#7, J7.pin3
  N4: Arduino_Nano.RESET, C3.+
  N5: Arduino_Nano.D10, J6.pin1
  N6: Arduino_Nano.D11/MOSI, J5.pin1
  N7: Arduino_Nano.D12/MISO, J4.pin1
  5V: Arduino_Nano.5V, ZIF28.VCC, J7.pin2
  N8: Arduino_Nano.D13/SCK, J3.pin1
  N9: ZIF28.RESET, J6.pin2
  N10: ZIF28.D0_(RX), J1.pin1
  N11: ZIF28.D1_(TX), J1.pin2
  N12: ZIF28.D2, J1.pin3
  N13: ZIF28.D3_(PWM), J1.pin4
  N14: ZIF28.D4, J7.pin1
  N15: ZIF28.D5_(PWM), J2.pin1
  N16: ZIF28.D6_(PWM), J2.pin2
  N17: ZIF28.D7, J2.pin3
  N18: ZIF28.D8, J2.pin4
  N19: ZIF28.D9_(PWM), J2.pin5
  N20: ZIF28.D10_(PWM), J2.pin6
  N21: ZIF28.D11_(PWM), J5.pin2
  N22: ZIF28.D12, J4.pin2
  N23: ZIF28.D13, J3.pin2

notes:
  D6
  D7
  D8
  6
  D9
  D10
  D5
  D11
  D12
  D13
  RST
  RX
  TX
  D2
  D3
  D4
  5v
  Gnd
