# Fritzing sketch ATmelProgrammer (saved by Fritzing 0.9.3b)
circuit board: 6.64301cm x 4.63223cm
breadboards: 1

parts:
  ZIF_SOCKET = Aries 28-6574-10 28W ZIF Socket [part_number=28-6574-10]
  XTAL1 = Crystal [frequency="16 Mhz" package=THT]
  C1 = Ceramic Capacitor [capacitance=22pF package="100 mil [THT, multilayer]"]
  C2 = Ceramic Capacitor [capacitance=22pF package="100 mil [THT, multilayer]"]
  Arduino_Nano = Arduino Nano (Rev3.0)
  C3 = Electrolytic Capacitor [capacitance=10µF package="100 mil [THT, electrolytic]"]
  SW3 = DIP SWITCH [package=dipswitch-02]
  SW1 = DIP SWITCH [package=dipswitch-02]
  SW2 = DIP SWITCH [package=dipswitch-02]
  J1 = female pin header, 2 pins [form="♀ (female)"]
  J2 = female pin header, 2 pins [form="♀ (female)"]
  J3 = female pin header, 2 pins [form="♀ (female)"]
  J4 = female pin header, 2 pins [form="♀ (female)"]
  J5 = female pin header, 2 pins [form="♀ (female)"]
  J6 = female pin header, 2 pins [form="♀ (female)"]

nets:
  N1: ZIF_SOCKET.Pin_1, SW1.2, J6.pin2
  N2: ZIF_SOCKET.Pin_4, SW1.1, J5.pin2
  N3: ZIF_SOCKET.Pin_7, Arduino_Nano.5V, SW3.1, J3.pin2
  N4: ZIF_SOCKET.Pin_8, C1.1, C2.0, Arduino_Nano.GND, SW1.4, J5.pin1
  N5: ZIF_SOCKET.Pin_9, XTAL1.pin_0, C1.0
  N6: ZIF_SOCKET.Pin_10, XTAL1.pin_1, C2.1
  N7: ZIF_SOCKET.Pin_17, Arduino_Nano.D11/MOSI, SW2.2, J2.pin2
  N8: ZIF_SOCKET.Pin_18, Arduino_Nano.D12/MISO, SW2.1, J1.pin2
  N9: ZIF_SOCKET.Pin_19, Arduino_Nano.D13/SCK, SW3.2, J4.pin2
  N10: ZIF_SOCKET.Pin_24, ZIF_SOCKET.Pin_26, SW2.4, J1.pin1
  N11: ZIF_SOCKET.Pin_25, SW2.3, J2.pin1
  N12: ZIF_SOCKET.Pin_27, SW3.3, J4.pin1
  N13: ZIF_SOCKET.Pin_28, SW3.4, J3.pin1
  N14: Arduino_Nano.RESET, C3.+
  N15: Arduino_Nano.D10, SW1.3, J6.pin1

notes:
  E
  A
  B
  C
  D
  F
  Jumpers/Switches
  Atmega328:
  All Off, except RST
  ATtiny85:
  All On
