# Fritzing sketch KidCalculator (saved by Fritzing 0.9.3b)
circuit board: 3.3217cm x 3.37261cm
breadboards: 1

parts:
  J1 = female pin header, 8 pins [form="♀ (female)"]
  10K = Resistor [tolerance=±5% resistance=10k package=THT]
  S3 = Pushbutton [package=THT]
  IC3 = IC, DIP package, 14 pins [chip_label=IC]
  J3 = female pin header, 2 pins [form="♀ (female)"]
  J4 = female pin header, 8 pins [form="♀ (female)"]
  J5 = female pin header, 1 pin [form="♀ (female)"]

nets:
  N1: J1.pin1, IC3.pin14, J3.pin2
  N2: J1.pin2, S3.leg0
  N3: J1.pin3, 10K.Pin_1, S3.leg1, IC3.pin1, J3.pin1
  N4: J1.pin4, IC3.pin9, J4.pin6
  N5: J1.pin5, IC3.pin10, J4.pin7
  N6: J1.pin6, IC3.pin11, J4.pin8
  N7: J1.pin7, IC3.pin12
  N8: J1.pin8, IC3.pin13
  N9: 10K.Pin_0, IC3.pin4, J5.pin1
  N10: IC3.pin3, J4.pin1
  N11: IC3.pin5, J4.pin4
  N12: IC3.pin6, J4.pin3
  N13: IC3.pin7, J4.pin2
  N14: IC3.pin8, J4.pin5

notes:
  RST
  CE
  DC
  DIN
  CLK
  VCC
  BL
  GND
  DIP switch
