# Fritzing sketch SerialToPCD8544-smt-dbg (saved by Fritzing 0.9.3b)
circuit board: 2.65253cm x 2.03567cm
breadboards: 1

parts:
  U2 = ATTINY45 [package=so]
  R1 = Resistor [tolerance=±5% resistance=10k package="0805 [SMD]"]
  J2 = female pin header, 3 pins [form="♀ (female)"]
  J3 = female pin header, 3 pins [form="♀ (female)"]
  S4 = Pushbutton [package=THT]
  J1 = female pin header, 8 pins [form="♀ (female)"]

nets:
  N1: U2.PB5(NRES), R1.Pin_0, J3.pin1
  N2: U2.PB3(ADC3), J1.pin6
  N3: U2.PB4(ADC2), J1.pin8
  N4: U2.GND, J2.pin1, J1.pin1, J1.pin7
  N5: U2.PB0(MOSI), J2.pin3
  N6: U2.PB1(MISO), J3.pin2, J1.pin4
  N7: U2.PB2(SCK_ADC1), J3.pin3, J1.pin5
  N8: U2.VCC, R1.Pin_1, J2.pin2, S4.leg1, J1.pin3
  N9: S4.leg0, J1.pin2

notes:
  RST
  CE
  DC
  DIN
  CLK
  VCC
  BL
  GND
