# Fritzing sketch TimerRelayLCD1602 (saved by Fritzing 0.9.3b)
circuit board: 6.44339cm x 4.20713cm
breadboards: 1

parts:
  LCD1602 = LCD screen [part_number=QY-1602A]
  Arduino_Nano = Arduino Nano (Rev3.0)
  R1 = Rotary Potentiometer (Large) [maximum_resistance=100kΩ package=THT]
  S2 = Pushbutton [package="[THT]"]
  S3 = Pushbutton [package="[THT]"]
  S4 = Pushbutton [package="[THT]"]
  Relay = female pin header, 3 pins [form="♀ (female)"]

nets:
  VSS: LCD1602.VSS, LCD1602.R/W, LCD1602.LED-, Arduino_Nano.GND, R1.leg1, S2.Pin_1, S2.Pin_2, S3.Pin_1, S3.Pin_2, S4.Pin_3, S4.Pin_4, Relay.pin1
  VDD: LCD1602.VDD, LCD1602.LED+, Arduino_Nano.5V, R1.leg2, Relay.pin2
  N1: LCD1602.V0, R1.wiper
  N2: LCD1602.RS, Arduino_Nano.D2
  N3: LCD1602.E, Arduino_Nano.D3
  N4: LCD1602.DB0, Arduino_Nano.D5
  N5: LCD1602.DB1, Arduino_Nano.D6
  N6: LCD1602.DB2, Arduino_Nano.D7
  N7: LCD1602.DB3, Arduino_Nano.D8
  N8: LCD1602.DB4, Arduino_Nano.D9
  N9: LCD1602.DB5, Arduino_Nano.D10
  N10: LCD1602.DB6, Arduino_Nano.D11/MOSI
  N11: LCD1602.DB7, Arduino_Nano.D12/MISO
  N12: Arduino_Nano.A3, Relay.pin3
  N13: Arduino_Nano.A2, S2.Pin_3, S2.Pin_4
  N14: Arduino_Nano.A1, S3.Pin_3, S3.Pin_4
  N15: Arduino_Nano.A0, S4.Pin_1, S4.Pin_2

notes:
  -
  +
  S
