# Fritzing sketch lcd12864 (saved by Fritzing 0.9.3b)
circuit board: 7.8991cm x 4.09006cm
breadboards: 1

parts:
  Arduino_Nano = Arduino Nano (Rev3.0)
  R1 = Rotary Potentiometer (Large) [maximum_resistance=100kΩ package=THT]
  GLCD_128x1 = 128 x 64 Graphic LCD
  J1 = female pin header, 11 pins [form="♀ (female)"]

nets:
  N1: Arduino_Nano.D1/TX, J1.pin1
  N2: Arduino_Nano.D0/RX, J1.pin2
  N3: Arduino_Nano.RESET, J1.pin5
  N4: Arduino_Nano.GND, R1.leg1, GLCD_128x1.1_Vss, GLCD_128x1.20_K(-), J1.pin4
  N5: Arduino_Nano.D4, GLCD_128x1.7_DB0
  N6: Arduino_Nano.D5, GLCD_128x1.8_DB1
  N7: Arduino_Nano.D6, GLCD_128x1.9_BD2
  N8: Arduino_Nano.D7, GLCD_128x1.10_DB3
  N9: Arduino_Nano.D8, GLCD_128x1.11_DB4
  N10: Arduino_Nano.D9, GLCD_128x1.12_DB5
  N11: Arduino_Nano.D10, GLCD_128x1.13_DB6
  N12: Arduino_Nano.D11/MOSI, GLCD_128x1.14_DB7
  N13: Arduino_Nano.VIN, J1.pin3
  N14: Arduino_Nano.5V, R1.leg2, GLCD_128x1.2_Vdd, GLCD_128x1.18_Vout, GLCD_128x1.19_A(+), J1.pin6
  N15: Arduino_Nano.A7, J1.pin7
  N16: Arduino_Nano.A6, J1.pin8
  N17: Arduino_Nano.A5, J1.pin9
  N18: Arduino_Nano.A4, J1.pin10
  N19: Arduino_Nano.A3, J1.pin11
  N20: Arduino_Nano.A2, GLCD_128x1.6_Enable
  N21: Arduino_Nano.A1, GLCD_128x1.5_R/W
  N22: Arduino_Nano.A0, GLCD_128x1.4_D/I
  N23: R1.wiper, GLCD_128x1.3_Vo
