# Fritzing sketch attiny84A-soic14-dip14-adapter (saved by Fritzing 0.9.3b)
circuit board: 2.17572cm x 1.94069cm

parts:
  IC4 = SO14 [chip_label=ATTiny24/44/84 package=SO]
  J1 = female pin header, 7 pins [form="♀ (female)"]
  J2 = female pin header, 7 pins [form="♀ (female)"]

nets:
  N1: IC4.1, J2.pin1
  N2: IC4.2, J2.pin2
  N3: IC4.3, J2.pin3
  N4: IC4.4, J2.pin4
  N5: IC4.5, J2.pin5
  N6: IC4.6, J2.pin6
  N7: IC4.7, J2.pin7
  N8: IC4.8, J1.pin7
  N9: IC4.9, J1.pin6
  N10: IC4.10, J1.pin5
  N11: IC4.11, J1.pin4
  N12: IC4.12, J1.pin3
  N13: IC4.13, J1.pin2
  N14: IC4.14, J1.pin1

notes:
  right wheel pwm out
  left wheel pwm out
  right wheel speed encoder IN
  serial cmd in
  +5V Gnd Gnd +12V
  left wheel speed encoder IN
  right wheel 0v
  left wheel 0v
  right wheel +12v
  left wheel +12v
  digital out 0-4 0v
  digital out 0-4 +12v
