# Fritzing sketch benchmark (saved by Fritzing 0.9.3b)
circuit board: 2.19991cm x 2.03084cm

parts:
  IC4 = SO14 [chip_label=ATTiny24/44/84 package=SO]
  U1 = atmega168 smd [package=tqfp]

nets:
  N1: IC4.9, U1.Pin_10
  N2: IC4.10, U1.Pin_9
  N3: IC4.12, U1.Pin_8
  N4: IC4.13, U1.Pin_7
  N5: IC4.14, U1.Pin_6

notes:
  right wheel pwm out
  left wheel pwm out
  right wheel speed encoder IN
  serial cmd in
  +5V Gnd Gnd +12V
  left wheel speed encoder IN
  right wheel 0v
  left wheel 0v
  right wheel +12v
  left wheel +12v
  digital out 0-4 0v
  digital out 0-4 +12v
  0.37mm drill diameter
