# Fritzing sketch esp8266-12e-AC-relay-v2 (saved by Fritzing 0.9.3b)
circuit board: 6.93271cm x 3.894cm
breadboards: 1

parts:
  U1 = ESP8266 WiFi Module [part_number=ESP8266]
  R2 = Resistor [tolerance=±5% resistance=10k package=THT]
  R3 = Resistor [tolerance=±5% resistance=10k package=THT]
  R4 = Resistor [tolerance=±5% resistance=10k package=THT]
  C8 = Ceramic Capacitor [capacitance=100nF package="100 mil [THT, multilayer]"]
  C7 = Ceramic Capacitor [capacitance=100nF package="100 mil [THT, multilayer]"]
  OMRON2 = OMRON PCB Power Relay – G5LE [part_number="G5LE-1\n" package=THT]
  B_C_E = female pin header, 3 pins [form="♀ (female)"]
  R5 = Resistor [tolerance=±5% resistance=10k package=THT]
  J11 = female pin header, 6 pins [form="♀ (female)"]
  J1 = female pin header, 8 pins [form="♀ (female)"]
  R1 = Resistor [tolerance=±5% resistance=10k package=THT]
  prog_/_run = female pin header, 3 pins [form="♀ (female)"]
  J12 = female pin header, 4 pins [form="♀ (female)"]
  J13 = female pin header, 2 pins [form="♀ (female)"]

nets:
  N1: U1.RXD, J12.pin4
  N2: U1.VCC, R2.Pin_1, R3.Pin_1, R4.Pin_1, OMRON2.COIL2, J1.pin1, R1.Pin_0, J12.pin2
  N3: U1.GPIO_0, prog_/_run.pin2
  N4: U1.GPIO_2, R3.Pin_0
  N5: U1.CH_PD, R2.Pin_0, C8.0, J1.pin6
  N6: U1.GND, C8.1, C7.1, B_C_E.pin1, prog_/_run.pin3, J12.pin1
  N7: U1.TXD, J12.pin3
  N8: U1.GPIO_4, J13.pin1
  N9: U1.GPIO_5, J13.pin2
  N10: U1.ADC_0, J1.pin7
  N11: U1.GPIO_16, J1.pin5
  N12: U1.GPIO_14, J1.pin4
  N13: U1.GPIO_12, J1.pin3
  N14: U1.GPIO_13, R5.Pin_0, J1.pin2
  N15: U1.REST, R4.Pin_0, C7.0, J1.pin8
  N16: OMRON2.A, J11.pin1
  N17: OMRON2.COIL1, B_C_E.pin2
  N18: OMRON2.C, J11.pin3, J11.pin4
  N19: OMRON2.B, J11.pin2
  N20: B_C_E.pin3, R5.Pin_1
  N21: J11.pin5, J11.pin6
  N22: R1.Pin_1, prog_/_run.pin1

notes:
  ~AC / L
  ~AC / N
  DC -
  DC +
  ~ AC Sw1
  ~ AC Sw2
