# Fritzing sketch esp8266-12e-AC-relay (saved by Fritzing 0.9.3b)
circuit board: 6.44573cm x 3.88932cm
breadboards: 1

parts:
  U1 = ESP8266 WiFi Module [part_number=ESP8266]
  J1 = female pin header, 8 pins [form="♀ (female)"]
  J2 = female pin header, 8 pins [form="♀ (female)"]
  R1 = Resistor [tolerance=±5% resistance=10k package=THT]
  R2 = Resistor [tolerance=±5% resistance=10k package=THT]
  R3 = Resistor [tolerance=±5% resistance=10k package=THT]
  R4 = Resistor [tolerance=±5% resistance=10k package=THT]
  C8 = Ceramic Capacitor [capacitance=100nF package="100 mil [THT, multilayer]"]
  C7 = Ceramic Capacitor [capacitance=100nF package="100 mil [THT, multilayer]"]
  OMRON2 = OMRON PCB Power Relay – G5LE [part_number="G5LE-1\n" package=THT]
  J12 = female pin header, 5 pins [form="♀ (female)"]
  J11 = female pin header, 5 pins [form="♀ (female)"]
  B_C_E = female pin header, 3 pins [form="♀ (female)"]
  R5 = Resistor [tolerance=±5% resistance=10k package=THT]
  R6 = Resistor [tolerance=±5% resistance=220 package=THT]

nets:
  N1: U1.RXD, J2.pin7
  N2: U1.VCC, J1.pin1, R1.Pin_0, R2.Pin_1, R3.Pin_1, R4.Pin_1, OMRON2.COIL2, J12.pin4
  N3: U1.GPIO_0, J2.pin4, J12.pin2
  N4: U1.GPIO_2, J2.pin3, R3.Pin_0
  N5: U1.CH_PD, J1.pin6, R2.Pin_0, C8.0
  N6: U1.GND, J2.pin1, C8.1, C7.1, J12.pin3, J12.pin5, B_C_E.pin1
  N7: U1.TXD, J2.pin8
  N8: U1.GPIO_15, J2.pin2
  N9: U1.GPIO_4, J2.pin6
  N10: U1.GPIO_5, J2.pin5
  N11: U1.ADC_0, J1.pin7
  N12: U1.GPIO_16, J1.pin5
  N13: U1.GPIO_14, J1.pin4
  N14: U1.GPIO_12, J1.pin3
  N15: U1.GPIO_13, J1.pin2, R5.Pin_0
  N16: U1.REST, J1.pin8, R4.Pin_0, C7.0
  N17: R1.Pin_1, J12.pin1
  N18: OMRON2.A, J11.pin1
  N19: OMRON2.COIL1, R6.Pin_1
  N20: OMRON2.C, J11.pin3
  N21: OMRON2.B, J11.pin2
  N22: J11.pin4, J11.pin5
  N23: B_C_E.pin2, R6.Pin_0
  N24: B_C_E.pin3, R5.Pin_1

notes:
  gnd-15
  prog/run
  ~AC / L
  ~AC / N
  DC -
  DC +
  ~ AC Sw1
  ~ AC Sw2
