# Fritzing sketch esp8266-12e (saved by Fritzing 0.9.3b)
circuit board: 3.44366cm x 4.03163cm
breadboards: 1

parts:
  U1 = ESP8266 WiFi Module [part_number=ESP8266]
  C3 = Electrolytic Capacitor [capacitance=0.22mF voltage=10V package="100 mil [THT, electrolytic]"]
  DC_In = Power plug
  J1 = female pin header, 8 pins [form="♀ (female)"]
  J2 = female pin header, 8 pins [form="♀ (female)"]
  U2 = V_REG_LD1117VXX [package=78xxl]
  C5 = Ceramic Capacitor [capacitance=100nF package="200 mil [THT, multilayer]"]
  J5 = female pin header, 3 pins [form="♀ (female)"]
  R1 = Resistor [tolerance=±5% resistance=220 package=THT]
  R2 = Resistor [tolerance=±5% resistance=220 package=THT]
  R3 = Resistor [tolerance=±5% resistance=220 package=THT]
  R4 = Resistor [tolerance=±5% resistance=220 package=THT]
  C6 = Ceramic Capacitor [capacitance=100nF package="100 mil [THT, multilayer]"]
  C7 = Ceramic Capacitor [capacitance=100nF package="100 mil [THT, multilayer]"]
  C8 = Ceramic Capacitor [capacitance=100nF package="100 mil [THT, multilayer]"]

nets:
  N1: U1.RXD, J2.pin7
  N2: U1.VCC, C3.+, J1.pin1, U2.OUT, R1.Pin_1, R2.Pin_1, R3.Pin_1, R4.Pin_1, C6.0
  N3: U1.GPIO_0, J2.pin4, J5.pin2
  N4: U1.GPIO_2, J2.pin3, R3.Pin_0
  N5: U1.CH_PD, J1.pin6, R2.Pin_0, C7.0
  GND: U1.GND, C3.-, DC_In.GND, J2.pin1, U2.GND, C5.1, J5.pin3, C6.1, C7.1, C8.1
  N6: U1.TXD, J2.pin8
  N7: U1.GPIO_15, J2.pin2
  N8: U1.GPIO_4, J2.pin6
  N9: U1.GPIO_5, J2.pin5
  N10: U1.ADC_0, J1.pin7
  N11: U1.GPIO_16, J1.pin5
  N12: U1.GPIO_14, J1.pin4
  N13: U1.GPIO_12, J1.pin3
  N14: U1.GPIO_13, J1.pin2
  N15: U1.REST, J1.pin8, R4.Pin_0, C8.0
  N16: DC_In.VCC, U2.IN, C5.0
  N17: J5.pin1, R1.Pin_0

notes:
  gnd-15
  prog
