# Fritzing sketch SmartCarController (saved by Fritzing 0.9.3b)
circuit board: 8.48026cm x 5.10226cm

parts:
  R1 = Resistor [tolerance=±5% resistance=10k package=THT]
  XTAL = Crystal [frequency="16 Mhz" package=THT]
  C1 = Ceramic Capacitor [capacitance=22pF package="200 mil [THT, multilayer]"]
  C2 = Ceramic Capacitor [capacitance=22pF package="200 mil [THT, multilayer]"]
  ULN_2003 = ULN2003A [package="DIP16 [THT]"]
  J2 = female pin header, 5 pins [form="♀ (female)"]
  J1 = female pin header, 6 pins [form="♀ (female)"]
  J3 = female pin header, 2 pins [form="♀ (female)"]
  R3 = Resistor [tolerance=±5% resistance=1k package=THT]
  L1 = LED - 5mm [color="Blue (525nm)" package="5 mm [THT]"]
  L2 = LED - 5mm [color="Green (570nm)" package="5 mm [THT]"]
  ATMega328PU = atmega328 [package=dip]
  J4 = female pin header, 6 pins [form="♀ (female)"]
  J5 = female pin header, 6 pins [form="♀ (female)"]
  J6 = female pin header, 6 pins [form="♀ (female)"]
  DC_12v_input = Power plug
  IN- = female pin header, 1 pin [form="♀ (female)"]
  IN+ = female pin header, 1 pin [form="♀ (female)"]
  78L05 = Voltage Regulator - 5V [package="TO220 [THT]"]
  R2 = Resistor [tolerance=±5% resistance=10k package=THT]
  ATTiny85 = attiny85 [package=dip]
  C3 = Tantalum Capacitor [capacitance=100nF package="100 mil [THT, tantalum]"]
  R4 = Resistor [tolerance=±5% resistance=1k package=THT]
  C4 = Electrolytic Capacitor [capacitance=470µF voltage=6.3V package="100 mil [THT, electrolytic]"]
  C5 = Ceramic Capacitor [capacitance=100nF package="100 mil [THT, multilayer]"]
  J7 = double row female pin header, 14 pins [form="♀ (female)"]
  J8 = double row female pin header, 6 pins [form="♀ (female)"]
  C6 = Ceramic Capacitor [capacitance=330nF package="100 mil [THT, multilayer]"]
  C7 = Electrolytic Capacitor [capacitance=470µF voltage=6.3V package="100 mil [THT, electrolytic]"]

nets:
  N1: R1.Pin_0, ATMega328PU.VCC, ATMega328PU.AVCC, ATMega328PU.AREF, J5.pin1, J5.pin2, J5.pin3, J5.pin4, J5.pin5, J5.pin6, 78L05.output_voltage, R2.Pin_0, ATTiny85.Pin_8, C3.+, R4.Pin_0, C4.+, C5.0, J8.pin2, J8.pin5
  N2: R1.Pin_1, ATMega328PU.RESET
  N3: XTAL.pin_0, C2.0, ATMega328PU.XLAT1
  N4: XTAL.pin_1, C1.1, ATMega328PU.XLAT2
  GND: C1.0, C2.1, ULN_2003.0V, L1.cathode, L2.cathode, ATMega328PU.GND, J4.pin1, J4.pin2, J4.pin3, J4.pin4, J4.pin5, J4.pin6, DC_12v_input.GND, IN-.pin1, 78L05.GND, ATTiny85.Pin_4, C3.-, C4.-, C5.1, J8.pin1, J8.pin6, C6.0, C7.-
  N5: ULN_2003.In_1, J2.pin2, ATMega328PU.D12
  N6: ULN_2003.In_2, J2.pin1, R3.Pin_1, ATMega328PU.D13
  N7: ULN_2003.In_3, J2.pin3, ATMega328PU.D11_(PWM)
  N8: ULN_2003.In_4, J2.pin4, ATMega328PU.D10_(PWM)
  N9: ULN_2003.In_5, J2.pin5, ATMega328PU.D9_(PWM)
  N10: ULN_2003.In_6, ATTiny85.Pin_3
  N11: ULN_2003.In_7, ATTiny85.Pin_2
  N12: ULN_2003.COM_-_Common, DC_12v_input.VCC, IN+.pin1, 78L05.input_voltage, J7.pin8, J7.pin9, J7.pin10, J7.pin11, J7.pin12, J7.pin13, J7.pin14, C6.1, C7.+
  N13: ULN_2003.Out_7, J7.pin7
  N14: ULN_2003.Out_6, J7.pin6
  N15: ULN_2003.Out_5, J7.pin5
  N16: ULN_2003.Out_4, J7.pin4
  N17: ULN_2003.Out_3, J7.pin3
  N18: ULN_2003.Out_2, J7.pin2
  N19: ULN_2003.Out_1, J7.pin1
  N20: J1.pin1, ATMega328PU.A5
  N21: J1.pin2, ATMega328PU.A4
  N22: J1.pin3, ATMega328PU.A3
  N23: J1.pin4, ATMega328PU.A2
  N24: J1.pin5, ATMega328PU.A1
  N25: J1.pin6, ATMega328PU.A0
  N26: J3.pin1, ATMega328PU.D1_(TX)
  N27: J3.pin2, ATMega328PU.D0_(RX)
  N28: R3.Pin_0, L1.anode
  N29: L2.anode, R4.Pin_1
  N30: ATMega328PU.D2, J6.pin4
  N31: ATMega328PU.D3_(PWM), J6.pin5
  N32: ATMega328PU.D4, J6.pin6
  N33: ATMega328PU.D5_(PWM), J6.pin1
  N34: ATMega328PU.D6_(PWM), J6.pin2
  N35: ATMega328PU.D7, J6.pin3
  N36: ATMega328PU.D8, ATTiny85.Pin_5
  N37: R2.Pin_1, ATTiny85.Pin_1
  N38: ATTiny85.Pin_6, J8.pin4
  N39: ATTiny85.Pin_7, J8.pin3

notes:
  right wheel pwm out
  left wheel pwm out
  right wheel speed encoder IN
  serial cmd in
  +5V Gnd Gnd +12V
  left wheel speed encoder IN
  right wheel 0v
  left wheel 0v
  right wheel +12v
  left wheel +12v
  digital out 0-4 0v
  digital out 0-4 +12v
  L
  PWM3
  PWM4
  PWM5
  PWM0
  PWM1
  PWM2
  R
  M0
  M1
  M2
  M3
  M4
  A0
  A1
  A2
  A3
  A4
  A5
  RX
  TX
  D0
  D1
  D2
  D3
  D4
  link
  XTAL=16Mhz
  C1=C2=22pF
  R1=R2=10KOhm
  J1 A/in
  J2 D/out
  J3 I/O
  J4 Gnd
  J6 PWM
  C3=C5=100nF
  C4=C7=470uF
  R3=R4=1KOhm
  L1=L2=led
  12V->USB
  J5 +5v
  J7 DC out
  J8 Speed In
  (c) B.A.T. Cave
  SMC v1.2
  12v to USB
  pwr con
  C6=330nF
