# Fritzing sketch PowerSupply (saved by Fritzing 0.9.3b)
circuit board: 3.28653cm x 2.94032cm

parts:
  DC_12v = Power plug
  USB+ = female pin header, 1 pin [form="♀ (female)"]
  SW = Pushbutton [package=THT]
  USB- = female pin header, 1 pin [form="♀ (female)"]
  C4 = Ceramic Capacitor [capacitance=100nF package="100 mil [THT, multilayer]"]
  C3 = Ceramic Capacitor [capacitance=330nF package="100 mil [THT, multilayer]"]
  78L05 = Voltage Regulator - 5V [package="TO220 [THT]"]
  J1 = female pin header, 3 pins [form="♀ (female)"]
  J2 = female pin header, 3 pins [form="♀ (female)"]
  C5 = Electrolytic Capacitor [capacitance=470µF package="100 mil [THT, electrolytic]"]
  C7 = Electrolytic Capacitor [capacitance=470µF package="100 mil [THT, electrolytic]"]

nets:
  GND: DC_12v.GND, USB-.pin1, C4.0, C3.0, 78L05.GND, J1.pin3, J2.pin1, C5.-, C7.-
  N1: DC_12v.VCC, SW.leg1
  N2: USB+.pin1, SW.leg0, C3.1, 78L05.input_voltage, J1.pin1, J2.pin3, C7.+
  N3: C4.1, 78L05.output_voltage, J1.pin2, J2.pin2, C5.+

notes:
  right wheel pwm out
  left wheel pwm out
  right wheel speed encoder IN
  serial cmd in
  +5V Gnd Gnd +12V
  left wheel speed encoder IN
  right wheel 0v
  left wheel 0v
  right wheel +12v
  left wheel +12v
  digital out 0-4 0v
  digital out 0-4 +12v
  12v->USB
  +12v
  +5v
  GND
