# Fritzing sketch SmartCarControllerHat-smt (saved by Fritzing 0.9.3b)
circuit board: 6.50052cm x 6.0891cm

parts:
  R1 = Resistor [tolerance=±5% resistance=10k package=THT]
  XTAL = Crystal [frequency="16 Mhz" package=THT]
  C1 = Ceramic Capacitor [capacitance=22pF package="200 mil [THT, multilayer]"]
  J2 = female pin header, 5 pins [form="♀ (female)"]
  J1 = female pin header, 6 pins [form="♀ (female)"]
  J4 = female pin header, 6 pins [form="♀ (female)"]
  J5 = female pin header, 6 pins [form="♀ (female)"]
  J6 = female pin header, 6 pins [form="♀ (female)"]
  DC_12v = Power plug
  USB+ = female pin header, 1 pin [form="♀ (female)"]
  C5 = Electrolytic Capacitor [capacitance=470µF voltage=6.3V package="100 mil [THT, electrolytic]"]
  S4 = Pushbutton [package=THT]
  C2 = Ceramic Capacitor [capacitance=22pF package="100 mil [THT, multilayer]"]
  J9 = double row female pin header, 6 pins [form="♀ (female)"]
  ATMega328PU = atmega328 [package=dip]
  RPi = Raspberry Pi 3 [part_number=RPI-3-V1.2]
  USB- = female pin header, 1 pin [form="♀ (female)"]
  C4 = Ceramic Capacitor [capacitance=100nF package="100 mil [THT, multilayer]"]
  C3 = Ceramic Capacitor [capacitance=330nF package="100 mil [THT, multilayer]"]
  78L05 = Voltage Regulator - 5V [package="TO220 [THT]"]
  C6 = Electrolytic Capacitor [capacitance=470µF package="100 mil [THT, electrolytic]"]
  L1 = LED - 5mm [color="Red (633nm)" package="5 mm [THT]"]
  R3 = Resistor [tolerance=±5% resistance=470 package=THT]
  IC5 = SO14 [chip_label=ATTiny24/44/84 package=SO]
  R4 = Resistor [tolerance=±5% resistance=10k package=THT]

nets:
  N1: R1.Pin_0, J5.pin1, J5.pin2, J5.pin3, J5.pin4, J5.pin5, J5.pin6, C5.+, J9.pin3, J9.pin4, ATMega328PU.VCC, ATMega328PU.AVCC, ATMega328PU.AREF, C4.1, 78L05.output_voltage, IC5.1
  N2: R1.Pin_1, ATMega328PU.RESET
  N3: XTAL.pin_0, C2.0, ATMega328PU.XLAT1
  N4: XTAL.pin_1, C1.1, ATMega328PU.XLAT2
  GND: C1.0, J4.pin1, J4.pin2, J4.pin3, J4.pin4, J4.pin5, J4.pin6, DC_12v.GND, C5.-, C2.1, J9.pin2, J9.pin5, ATMega328PU.GND, USB-.pin1, C4.0, C3.0, 78L05.GND, L1.cathode, IC5.14, R4.Pin_1
  N5: J2.pin1, ATMega328PU.D13, R3.Pin_0
  N6: J2.pin2, ATMega328PU.D12
  N7: J2.pin3, ATMega328PU.D11_(PWM)
  N8: J2.pin4, ATMega328PU.D10_(PWM)
  N9: J2.pin5, ATMega328PU.D9_(PWM)
  N10: J1.pin1, ATMega328PU.A5
  N11: J1.pin2, ATMega328PU.A4
  N12: J1.pin3, ATMega328PU.A3
  N13: J1.pin4, ATMega328PU.A2
  N14: J1.pin5, ATMega328PU.A1
  N15: J1.pin6, ATMega328PU.A0
  N16: J6.pin1, ATMega328PU.D5_(PWM)
  N17: J6.pin2, ATMega328PU.D6_(PWM)
  N18: J6.pin3, ATMega328PU.D7
  N19: J6.pin4, ATMega328PU.D2
  N20: J6.pin5, ATMega328PU.D3_(PWM)
  N21: J6.pin6, ATMega328PU.D4
  N22: DC_12v.VCC, S4.leg1
  N23: USB+.pin1, S4.leg0, C3.1, 78L05.input_voltage, C6.+
  N24: J9.pin1, IC5.2
  N25: J9.pin6, IC5.3
  N26: ATMega328PU.D0_(RX), RPi.GPIO14
  N27: ATMega328PU.D1_(TX), RPi.GPIO15
  N28: ATMega328PU.D8, IC5.7
  N29: L1.anode, R3.Pin_1
  N30: IC5.4, R4.Pin_0

notes:
  right wheel pwm out
  left wheel pwm out
  right wheel speed encoder IN
  serial cmd in
  +5V Gnd Gnd +12V
  left wheel speed encoder IN
  right wheel 0v
  left wheel 0v
  right wheel +12v
  left wheel +12v
  digital out 0-4 0v
  digital out 0-4 +12v
  link
  12v->USB
