# Fritzing sketch SmartCarControllerHat-v2 (saved by Fritzing 0.9.3b)
circuit board: 6.50052cm x 6.0891cm

parts:
  R1 = Resistor [tolerance=±5% resistance=10k package=THT]
  XTAL = Crystal [frequency="16 Mhz" package=THT]
  C1 = Ceramic Capacitor [capacitance=22pF package="200 mil [THT, multilayer]"]
  INPUT = female pin header, 6 pins [form="♀ (female)"]
  J4 = female pin header, 6 pins [form="♀ (female)"]
  J5 = female pin header, 6 pins [form="♀ (female)"]
  J6 = female pin header, 6 pins [form="♀ (female)"]
  DC_12v = Power plug
  USB+ = female pin header, 1 pin [form="♀ (female)"]
  C5 = Electrolytic Capacitor [capacitance=470µF voltage=6.3V package="100 mil [THT, electrolytic]"]
  S4 = Pushbutton [package=THT]
  C2 = Ceramic Capacitor [capacitance=22pF package="100 mil [THT, multilayer]"]
  ATMega328PU = atmega328 [package=dip]
  RPi = Raspberry Pi 3 [part_number=RPI-3-V1.2]
  USB- = female pin header, 1 pin [form="♀ (female)"]
  C4 = Ceramic Capacitor [capacitance=100nF package="100 mil [THT, multilayer]"]
  C3 = Ceramic Capacitor [capacitance=330nF package="100 mil [THT, multilayer]"]
  78L05 = Voltage Regulator - 5V [package="TO220 [THT]"]
  C6 = Electrolytic Capacitor [capacitance=470µF package="100 mil [THT, electrolytic]"]
  L293D = L293D [package=THT]
  J7 = double row female pin header, 8 pins [form="♀ (female)"]
  IC2 = IC, DIP package, 14 pins [chip_label=IC]
  J8 = double row female pin header, 6 pins [form="♀ (female)"]
  R2 = Resistor [tolerance=±5% resistance=10k package=THT]

nets:
  N1: R1.Pin_0, J5.pin1, J5.pin2, J5.pin3, J5.pin4, J5.pin5, J5.pin6, C5.+, ATMega328PU.VCC, ATMega328PU.AVCC, ATMega328PU.AREF, C4.1, 78L05.output_voltage, L293D.Enable_1, L293D.Enable_2, L293D.+V, IC2.pin1, J8.pin2, J8.pin5, R2.Pin_0
  N2: R1.Pin_1, ATMega328PU.RESET
  N3: XTAL.pin_0, C2.0, ATMega328PU.XLAT1
  N4: XTAL.pin_1, C1.1, ATMega328PU.XLAT2
  GND: C1.0, J4.pin1, J4.pin2, J4.pin3, J4.pin4, J4.pin5, J4.pin6, DC_12v.GND, C5.-, C2.1, ATMega328PU.GND, USB-.pin1, C4.0, C3.0, 78L05.GND, C6.-, L293D.0V, J7.pin5, J7.pin6, J7.pin7, J7.pin8, IC2.pin14, J8.pin1, J8.pin6
  N5: INPUT.pin1, ATMega328PU.A5
  N6: INPUT.pin2, ATMega328PU.A4
  N7: INPUT.pin3, ATMega328PU.A3
  N8: INPUT.pin4, ATMega328PU.A2
  N9: INPUT.pin5, ATMega328PU.A1
  N10: INPUT.pin6, ATMega328PU.A0
  N11: J6.pin1, ATMega328PU.D5_(PWM)
  N12: J6.pin2, ATMega328PU.D6_(PWM)
  N13: J6.pin3, ATMega328PU.D7
  N14: J6.pin4, ATMega328PU.D2
  N15: J6.pin5, ATMega328PU.D3_(PWM)
  N16: J6.pin6, ATMega328PU.D4
  N17: DC_12v.VCC, S4.leg1
  N18: USB+.pin1, S4.leg0, C3.1, 78L05.input_voltage, C6.+, L293D.+Vmotor
  N19: ATMega328PU.D0_(RX), RPi.GPIO14
  N20: ATMega328PU.D1_(TX), RPi.GPIO15
  N21: ATMega328PU.D8, IC2.pin10
  N22: L293D.In_1, IC2.pin6
  N23: L293D.Out_1_(_Controlled_by_Enable_1_), J7.pin3
  N24: L293D.Out_2_(_Controlled_by_Enable_1_), J7.pin2
  N25: L293D.In_2, IC2.pin8
  N26: L293D.In_3, IC2.pin9
  N27: L293D.Out_3_(_Controlled_by_Enable_2_), J7.pin1
  N28: L293D.Out_4_(_Controlled_by_Enable_2_), J7.pin4
  N29: L293D.In_4, IC2.pin7
  N30: IC2.pin2, J8.pin3
  N31: IC2.pin3, J8.pin4
  N32: IC2.pin4, R2.Pin_1

notes:
  right wheel pwm out
  left wheel pwm out
  right wheel speed encoder IN
  serial cmd in
  +5V Gnd Gnd +12V
  left wheel speed encoder IN
  right wheel 0v
  left wheel 0v
  right wheel +12v
  left wheel +12v
  digital out 0-4 0v
  digital out 0-4 +12v
  link
  12v->USB
