# Fritzing sketch SmartCarControllerHat2Sided (saved by Fritzing 0.9.3b)
circuit board: 6.50052cm x 6.0891cm

parts:
  R1 = Resistor [tolerance=±5% resistance=10k package=THT]
  XTAL = Crystal [frequency="16 Mhz" package=THT]
  C1 = Ceramic Capacitor [capacitance=22pF package="200 mil [THT, multilayer]"]
  ULN_2003 = ULN2003A [package="DIP16 [THT]"]
  J2 = female pin header, 5 pins [form="♀ (female)"]
  J1 = female pin header, 6 pins [form="♀ (female)"]
  J4 = female pin header, 6 pins [form="♀ (female)"]
  J5 = female pin header, 6 pins [form="♀ (female)"]
  J6 = female pin header, 6 pins [form="♀ (female)"]
  DC_12v = Power plug
  USB+ = female pin header, 1 pin [form="♀ (female)"]
  C5 = Electrolytic Capacitor [capacitance=470µF voltage=6.3V package="100 mil [THT, electrolytic]"]
  J7 = double row female pin header, 14 pins [form="♀ (female)"]
  S4 = Pushbutton [package=THT]
  C2 = Ceramic Capacitor [capacitance=22pF package="100 mil [THT, multilayer]"]
  ATTiny85 = attiny85 [package=dip]
  J9 = double row female pin header, 6 pins [form="♀ (female)"]
  ATMega328PU = atmega328 [package=dip]
  RPi = Raspberry Pi 3 [part_number=RPI-3-V1.2]
  R2 = Resistor [tolerance=±5% resistance=10k package=THT]
  USB- = female pin header, 1 pin [form="♀ (female)"]
  C4 = Ceramic Capacitor [capacitance=100nF package="100 mil [THT, multilayer]"]
  C3 = Ceramic Capacitor [capacitance=330nF package="100 mil [THT, multilayer]"]
  78L05 = Voltage Regulator - 5V [package="TO220 [THT]"]
  C6 = Electrolytic Capacitor [capacitance=470µF package="100 mil [THT, electrolytic]"]
  L1 = LED - 5mm [color="Red (633nm)" package="5 mm [THT]"]
  R3 = Resistor [tolerance=±5% resistance=470 package=THT]

nets:
  N1: R1.Pin_0, ATTiny85.Pin_8, J9.pin3, J9.pin4, ATMega328PU.VCC, ATMega328PU.AVCC, ATMega328PU.AREF, R2.Pin_1, C4.1, 78L05.output_voltage
  N2: R1.Pin_1, ATMega328PU.RESET
  N3: XTAL.pin_0, C2.0, ATMega328PU.XLAT1
  N4: XTAL.pin_1, C1.1, ATMega328PU.XLAT2
  GND: C1.0, ULN_2003.0V, J4.pin1, J4.pin2, J4.pin3, J4.pin4, J4.pin5, J4.pin6, DC_12v.GND, C5.-, C2.1, ATTiny85.Pin_4, J9.pin2, J9.pin5, ATMega328PU.GND, USB-.pin1, C4.0, C3.0, 78L05.GND, C6.-, L1.cathode
  N5: ULN_2003.In_1, J2.pin1, ATMega328PU.D13, R3.Pin_0
  N6: ULN_2003.In_2, J2.pin2, ATMega328PU.D12
  N7: ULN_2003.In_3, J2.pin3, ATMega328PU.D11_(PWM)
  N8: ULN_2003.In_4, J2.pin4, ATMega328PU.D10_(PWM)
  N9: ULN_2003.In_5, J2.pin5, ATMega328PU.D9_(PWM)
  N10: ULN_2003.In_6, ATTiny85.Pin_3
  N11: ULN_2003.In_7, ATTiny85.Pin_2
  N12: ULN_2003.COM_-_Common, USB+.pin1, J7.pin8, J7.pin9, J7.pin10, J7.pin11, J7.pin12, J7.pin13, J7.pin14, S4.leg0, C3.1, 78L05.input_voltage, C6.+
  N13: ULN_2003.Out_7, J7.pin7
  N14: ULN_2003.Out_6, J7.pin6
  N15: ULN_2003.Out_5, J7.pin5
  N16: ULN_2003.Out_4, J7.pin4
  N17: ULN_2003.Out_3, J7.pin3
  N18: ULN_2003.Out_2, J7.pin2
  N19: ULN_2003.Out_1, J7.pin1
  N20: J1.pin1, ATMega328PU.A5
  N21: J1.pin2, ATMega328PU.A4
  N22: J1.pin3, ATMega328PU.A3
  N23: J1.pin4, ATMega328PU.A2
  N24: J1.pin5, ATMega328PU.A1
  N25: J1.pin6, ATMega328PU.A0
  N26: J5.pin1, J5.pin2, J5.pin3, J5.pin4, J5.pin5, J5.pin6, C5.+
  N27: J6.pin1, ATMega328PU.D5_(PWM)
  N28: J6.pin2, ATMega328PU.D6_(PWM)
  N29: J6.pin3, ATMega328PU.D7
  N30: J6.pin4, ATMega328PU.D2
  N31: J6.pin5, ATMega328PU.D3_(PWM)
  N32: J6.pin6, ATMega328PU.D4
  N33: DC_12v.VCC, S4.leg1
  N34: ATTiny85.Pin_1, R2.Pin_0
  N35: ATTiny85.Pin_5, ATMega328PU.D8
  N36: ATTiny85.Pin_6, J9.pin1
  N37: ATTiny85.Pin_7, J9.pin6
  N38: ATMega328PU.D0_(RX), RPi.GPIO14
  N39: ATMega328PU.D1_(TX), RPi.GPIO15
  N40: L1.anode, R3.Pin_1

notes:
  right wheel pwm out
  left wheel pwm out
  right wheel speed encoder IN
  serial cmd in
  +5V Gnd Gnd +12V
  left wheel speed encoder IN
  right wheel 0v
  left wheel 0v
  right wheel +12v
  left wheel +12v
  digital out 0-4 0v
  digital out 0-4 +12v
  link
  12v->USB
