# Fritzing sketch lcd1602 (saved by Fritzing 0.9.3b)
circuit board: 5.6972cm x 4.1861cm
breadboards: 1

parts:
  LCD1602 = LCD screen [part_number=QY-1602A]
  Arduino_Nano = Arduino Nano (Rev3.0)
  R1 = Rotary Potentiometer (Large) [maximum_resistance=100kΩ package=THT]
  J1 = female pin header, 11 pins [form="♀ (female)"]

nets:
  VSS: LCD1602.VSS, LCD1602.R/W, LCD1602.LED-, Arduino_Nano.GND, R1.leg1, J1.pin2
  VDD: LCD1602.VDD, LCD1602.LED+, Arduino_Nano.5V, R1.leg2, J1.pin4
  N1: LCD1602.V0, R1.wiper
  N2: LCD1602.RS, Arduino_Nano.D2
  N3: LCD1602.E, Arduino_Nano.D3
  N4: LCD1602.DB0, Arduino_Nano.D5
  N5: LCD1602.DB1, Arduino_Nano.D6
  N6: LCD1602.DB2, Arduino_Nano.D7
  N7: LCD1602.DB3, Arduino_Nano.D8
  N8: LCD1602.DB4, Arduino_Nano.D9
  N9: LCD1602.DB5, Arduino_Nano.D10, J1.pin9
  N10: LCD1602.DB6, Arduino_Nano.D11/MOSI, J1.pin10
  N11: LCD1602.DB7, Arduino_Nano.D12/MISO, J1.pin11
  N12: Arduino_Nano.D1/TX, J1.pin6
  N13: Arduino_Nano.D0/RX, J1.pin7
  N14: Arduino_Nano.RESET, J1.pin3
  N15: Arduino_Nano.D4, J1.pin8
  N16: Arduino_Nano.VIN, J1.pin1
  N17: Arduino_Nano.D13/SCK, J1.pin5
